# Fritzing sketch hardware_diagram (saved by Fritzing 1.0.6)
breadboards: 1

parts:
  Raspberry_Pi_1 = Raspberry Pi 3 [part_number=RPI-3-V1.2]
  S2 = 0.91 inch OLED I2C Display 128 x 32 Pixels
  RE2 = KY-040 Rotary encoder [package=THT]
  M1 = RioRand LM2596
  Part4 = I2C level shifter bidirectional
  Part5 = Thermal Printer
  C22 = Electrolytic Capacitor [capacitance=1000µF voltage=35V package="300 mil [THT, electrolytic]"]
  U1 = SWITCH-SPST-2 [package=switch-spst-vertical]
  V1 = DC Power Supply [voltage=9V internal_resistance=0.1Ω max_current=6A]  # not connected

nets:
  3V3: Raspberry_Pi_1.3v3, Raspberry_Pi_1.3V3, S2.VCC, RE2.Vcc, Part4.LV
  N1: Raspberry_Pi_1.GPIO2, S2.SDA
  N2: Raspberry_Pi_1.GPIO3, S2.SCL
  N3: Raspberry_Pi_1.GPIO5, RE2.SW
  N4: Raspberry_Pi_1.GPIO6, RE2.DT
  N5: Raspberry_Pi_1.GPIO13, RE2.CLK
  GND: Raspberry_Pi_1.GND, S2.GND, RE2.GND, M1.Pin_2, M1.Pin_4, Part4.GND, Part5.GND, C22.-
  N6: Raspberry_Pi_1.GPIO15, Part4.LV1
  N7: Raspberry_Pi_1.GPIO14, Part4.LV2
  N8: Raspberry_Pi_1.5V, M1.Pin_3, Part4.HV
  N9: M1.Pin_1, Part5.VH, C22.+, U1.O
  N10: Part4.HV1, Part5.TXD
  N11: Part4.HV2, Part5.RXD

custom parts:
  KY-040 Rotary encoder: KY-040 Rotary Encoder with switch on breakout borad from AZ Delivery
